# Fritzing sketch arduino_post_request (saved by Fritzing 0.8.3b)
breadboards: 1

parts:
  Part3 = Arduino Ethernet Shield (Rev3)
  RHT1 = Humidity and Temperature Sensor RHT03

nets:
  N1: Part3.PWM_D5, RHT1.Data-signal
  5V: Part3.5V, RHT1.Vcc
  N2: Part3.GND, RHT1.GND_2
